// Logisim project 1_1Logisim.circ as structural Verilog: 5 circuits, main circuit main
module main (
  input  x1,
  input  x2,
  input  x3,
  input  x4,
  input  x5,
  input  D0,
  input  S0,
  input  D1,
  output y1,
  output y2,
  output y3,
  output y4
);

  NOT_Gatter not_gatter_1 (.x1(x1), .y1(y1));
  AND_Gatter and_gatter_1 (.x1(x2), .x2(x3), .y1(y2));
  OR_Gatter or_gatter_1 (.x1(x4), .x2(x5), .y1(y3));
  Multiplexer multiplexer_1 (.D0(D0), .S0(S0), .D1(D1), .y1(y4));
endmodule

// 1
module NOT_Gatter (
  input  x1,
  output y1
);

  nand nand_1 (y1, x1, x1);
endmodule

// &
module AND_Gatter (
  input  x1,
  input  x2,
  output y1
);

  wire nand_1_out;

  nand nand_1 (nand_1_out, x1, x2);
  not nand_2 (y1, nand_1_out);  // NAND_Gate
endmodule

// >=1
module OR_Gatter (
  input  x1,
  input  x2,
  output y1
);

  wire nand_1_out, nand_2_out;

  nand nand_1 (nand_1_out, x1, x1);
  nand nand_2 (nand_2_out, x2, x2);
  nand nand_3 (y1, nand_1_out, nand_2_out);
endmodule

// MUX
module Multiplexer (
  input  D0,
  input  S0,
  input  D1,
  output y1
);

  wire and_1_out, and_2_out, not_1_out;

  not not_1 (not_1_out, S0);
  and and_1 (and_1_out, D0, not_1_out);
  and and_2 (and_2_out, S0, D1);
  or or_1 (y1, and_1_out, and_2_out);
endmodule
